# Fritzing sketch Rube-Goldberg (saved by Fritzing 0.9.3b)
breadboards: 1

parts:
  Photocell = PHOTOCELL [package=photocell]
  LED1 = LEDs [package=led10mm]
  Marble_Switch = SWITCH-MOMENTARY-2 [package=tactile_switch_tall]
  Marble_Motor = DC Motor
  2N27000 = Basic FET P-Channel [package="DPak [SMD]"]
  R3 = Resistor [tolerance=±5% resistance=1k package="2512 [SMD]"]
  R4 = Resistor [tolerance=±5% resistance=100 package="2512 [SMD]"]
  Flyback = Rectifier Diode [part_number=1N4001 package="300 mil [THT]"]
  Piezo_Buzzer = Piezo Speaker
  R5 = Resistor [tolerance=±5% resistance=100 package="2512 [SMD]"]
  R6 = Resistor [tolerance=±5% resistance=10k package="2512 [SMD]"]
  R7 = Rotary Potentiometer (Small) [maximum_resistance=100kΩ package=THT]
  L031K6 = STM32 Nucleo boards
  2N27000_2 = Basic FET P-Channel [package="DPak [SMD]"]
  U1 = LIPO-1000mAh [package=lipo-1000]
  Mic_Ciruit = mystery part, 3 pins [chip_label=TBD]
  U2 = Voltage Regulator - 5V [package="TO220 [THT]"]

nets:
  3.3V: Photocell.P$1, Marble_Switch.2, R7.leg2, L031K6.3V3, Mic_Ciruit.pin1
  N1: Photocell.P$2, R6.Pin_0, L031K6.A2
  GND: LED1.C, 2N27000.source, R3.Pin_0, Piezo_Buzzer.pin2, R5.Pin_0, R6.Pin_1, R7.wiper, 2N27000_2.source, U1.-, Mic_Ciruit.pin2, U2.GND
  N2: LED1.A, R4.Pin_0
  N3: Marble_Switch.1, R5.Pin_1, L031K6.D6_PWM
  2S Lipo: Marble_Motor.pin_1, Flyback.cathode, U1.+, U2.input_voltage
  N4: Marble_Motor.pin_2, 2N27000.drain, Flyback.anode, 2N27000_2.drain
  D5: 2N27000.Gate, R3.Pin_1, L031K6.D5_PWM, 2N27000_2.Gate
  N5: R4.Pin_1, L031K6.D7
  N6: Piezo_Buzzer.pin1, L031K6.D2
  N7: R7.leg1, L031K6.A1
  N8: L031K6.A0, Mic_Ciruit.pin3
  N9: L031K6.VIN, U2.output_voltage
